# Fritzing sketch timelapse (saved by Fritzing 0.7.5b)
breadboards: 1

parts:
  Arduino1 = Arduino
  U1 = Optocoupler [package=THT]
  U2 = Optocoupler [package=THT]
  R1 = Resistor [tolerance=±5% resistance=1k package=THT]
  J1 = Basic Servo
  VCC1 = 4 x AAA Battery Mount
  VCC2 = Battery block 9V
  R2 = Resistor [tolerance=±5% resistance=1k package=THT]
  U3 = mystery part, 3 pins [chip_label=Kamera spacing=300mil]
  LED1 = LED - 5mm [color="Red (633nm)" package="5 mm [THT]"]
  LED2 = LED - 5mm [color="Yellow (595nm)" package="5 mm [THT]"]
  R3 = Rotary Potentiometer (Small) [maximum_resistance=100kΩ]
  LED3 = LED - 5mm [color="White (4500K)" package="5 mm [THT]"]
  LED4 = LED - 5mm [color="Blue (525nm)" package="5 mm [THT]"]
  S3 = Pushbutton [package=THT]
  S4 = Pushbutton [package=THT]
  R5 = Resistor [tolerance=±5% resistance=220 package=THT]
  R6 = Resistor [tolerance=±5% resistance=220 package=THT]
  R7 = Resistor [tolerance=±5% resistance=220 package=THT]
  R8 = Resistor [tolerance=±5% resistance=220 package=THT]
  Part1 = EasyDriver_v44
  M1 = Stepper Motor - Bipolar

nets:
  N1: Arduino1.D13, Part1.SLEEP
  N2: Arduino1.D12, S4.leg1
  N3: Arduino1.D11, Part1.STEP
  N4: Arduino1.D10, Part1.DIR
  N5: Arduino1.D9, J1.pulse
  N6: Arduino1.D8, LED3.anode
  N7: Arduino1.D7, LED4.anode
  N8: Arduino1.D6, S3.leg1
  N9: Arduino1.D4, LED2.anode
  N10: Arduino1.D3, R2.Pin_0
  N11: Arduino1.D2, LED1.anode
  N12: Arduino1.+5V, R3.leg1
  GND: Arduino1.GND, U1.Pin_2, U2.Pin_2, J1.gnd, VCC1.-, VCC2.-, R3.leg2, R5.Pin_0, R6.Pin_0, R7.Pin_0, R8.Pin_0, Part1.GND, Part1.MS2
  N13: Arduino1.VIN, VCC2.+, S3.leg0, S4.leg0, Part1.V+
  N14: Arduino1.A2, R3.wiper
  N15: U1.Pin_1, R1.Pin_1
  N16: U1.Pin_4, U3.pin3
  N17: U1.Pin_5, U2.Pin_5, U3.pin1
  N18: U2.Pin_1, R2.Pin_1
  N19: U2.Pin_4, U3.pin2
  N20: J1.vcc, VCC1.+
  N21: Part1.OUT2A, M1.A
  N22: Part1.OUT2B, M1.C
  N23: Part1.OUT1A, M1.B
  N24: Part1.OUT1B, M1.D

notes:
  Arduino power (needed for 5v, the rechargeable will not regulate to 5v)
  8 pack AA (8x1.5=12v)
  Servo Power
  4 pack AA (4x1.5=6v)
  Optocouplers will connect the camera internal circuit (shared ground)
  [Servo drives timelapse Sled
  Both power supplies share the same ground (so the arduino can send the pulse to the servo)
